// Digital circuit UTS NO 11.dig as structural Verilog
module UTS_NO_11 (
  input  X,
  input  Y,
  input  Z,
  output P
);

  wire and_1_out, and_2_out, and_3_out, and_4_out, not_1_out, not_2_out, not_3_out;

  not not_1 (not_1_out, X);
  not not_2 (not_2_out, Y);
  not not_3 (not_3_out, Z);
  and and_1 (and_1_out, not_1_out, not_2_out, Z);
  and and_2 (and_2_out, X, Y, not_3_out);
  and and_3 (and_3_out, not_1_out, Y, Z);
  and and_4 (and_4_out, not_1_out, Y);
  or or_1 (P, and_3_out, and_1_out, and_2_out, and_4_out);

  // Notes on the sheet:
  //   FIKRI NUR ALIM
  //   11.w'y'z + wyz' + x'yz + xy
endmodule
